# Fritzing sketch rpi_wiring_scheme (saved by Fritzing 0.9.3b)
breadboards: 1

parts:
  Raspberry_Pi_1 = Raspberry Pi 3 [part_number=RPI-3-V1.2]
  RHT1 = Humidity and Temperature Sensor RHT03
  LED1 = LEDs [package=led10mm]
  R1 = Resistor [tolerance=±5% resistance=470 package="1206 [SMD]"]
  R2 = Resistor [tolerance=±5% resistance=4.7k package="1206 [SMD]"]

nets:
  N1: Raspberry_Pi_1.GND, RHT1.GND_2, LED1.C
  N2: Raspberry_Pi_1.GPIO18, R1.Pin_0
  N3: Raspberry_Pi_1.GPIO14, RHT1.Data-signal, R2.Pin_1
  5V: Raspberry_Pi_1.5V, RHT1.Vcc, R2.Pin_0
  N4: LED1.A, R1.Pin_1

notes:
  DH-11 Sensor
  VCC | Signal | X | GND
  DH-11 Resistor : 4.7k
  LED Resistor : 470Ω
